// Logisim project Assignment1.circ as structural Verilog: 3 circuits, main circuit main
module main (
);

  wire Clock_out, Controller_state_1_pin, Controller_state_2_pin, Controller_state_3_pin,
       Controller_state_4_pin, Controller_state_5_pin;
  wire [3:0] Counter_output;

  Clock Clock (.out(Clock_out));
  Counter Counter (.\input (Clock_out), .\output (Counter_output));
  Controller Controller (
    .\input (Counter_output), .State_3_pin(Controller_state_3_pin), .State_2_pin(Controller_state_2_pin),
    .State_1_pin(Controller_state_1_pin), .State_4_pin(Controller_state_4_pin),
    .State_5_pin(Controller_state_5_pin));
  LED led_1 (.in(Controller_state_1_pin));
  LED led_2 (.in(Controller_state_1_pin));
  LED led_3 (.in(Controller_state_1_pin));
  LED led_4 (.in(Controller_state_1_pin));
  LED led_5 (.in(Controller_state_1_pin));
  LED led_6 (.in(Controller_state_1_pin));
  LED led_7 (.in(Controller_state_1_pin));
  LED led_8 (.in(Controller_state_1_pin));
  LED led_9 (.in(Controller_state_1_pin));
  LED led_10 (.in(Controller_state_1_pin));
  LED led_11 (.in(Controller_state_1_pin));
  LED led_12 (.in(Controller_state_1_pin));
  LED led_13 (.in(Controller_state_1_pin));
  LED led_14 (.in(Controller_state_1_pin));
  LED led_15 (.in(Controller_state_1_pin));
  LED led_16 (.in(Controller_state_1_pin));
  LED led_17 (.in(Controller_state_1_pin));
  LED led_18 (.in(Controller_state_2_pin));
  LED led_19 (.in(Controller_state_2_pin));
  LED led_20 (.in(Controller_state_1_pin));
  LED led_21 (.in(Controller_state_1_pin));
  LED led_22 (.in(Controller_state_1_pin));
  LED led_23 (.in(Controller_state_1_pin));
  LED led_24 (.in(Controller_state_2_pin));
  LED led_25 (.in(Controller_state_2_pin));
  LED led_26 (.in(Controller_state_3_pin));
  LED led_27 (.in(Controller_state_3_pin));
  LED led_28 (.in(Controller_state_2_pin));
  LED led_29 (.in(Controller_state_2_pin));
  LED led_30 (.in(Controller_state_2_pin));
  LED led_31 (.in(Controller_state_2_pin));
  LED led_32 (.in(Controller_state_2_pin));
  LED led_33 (.in(Controller_state_3_pin));
  LED led_34 (.in(Controller_state_3_pin));
  LED led_35 (.in(Controller_state_4_pin));
  LED led_36 (.in(Controller_state_3_pin));
  LED led_37 (.in(Controller_state_3_pin));
  LED led_38 (.in(Controller_state_3_pin));
  LED led_39 (.in(Controller_state_3_pin));
  LED led_40 (.in(Controller_state_4_pin));
  LED led_41 (.in(Controller_state_5_pin));
  LED led_42 (.in(Controller_state_4_pin));
  LED led_43 (.in(Controller_state_4_pin));
  LED led_44 (.in(Controller_state_4_pin));
  LED led_45 (.in(Controller_state_3_pin));
  LED led_46 (.in(Controller_state_4_pin));
  LED led_47 (.in(Controller_state_4_pin));
  LED led_48 (.in(Controller_state_4_pin));
  LED led_49 (.in(Controller_state_5_pin));
  LED led_50 (.in(Controller_state_5_pin));
  LED led_51 (.in(Controller_state_5_pin));
  LED led_52 (.in(Controller_state_5_pin));
  LED led_53 (.in(Controller_state_4_pin));
  LED led_54 (.in(Controller_state_5_pin));
  LED led_55 (.in(Controller_state_5_pin));
  LED led_56 (.in(Controller_state_5_pin));
  LED led_57 (.in(Controller_state_5_pin));
endmodule

module Counter (
  input  \input ,
  output [3:0] \output 
);

  wire _14_out, bit_1_qn, bit_2_qn, bit_3_qn, bit_4_qn, not_1_out;

  D_Flip_Flop bit_1 (.clk(\input ), .D(bit_1_qn), .Q(\output [0]), .Qn(bit_1_qn), .reset(_14_out));  // open: preset, en
  D_Flip_Flop bit_2 (
    .clk(bit_1_qn), .D(bit_2_qn), .Q(\output [1]), .Qn(bit_2_qn), .reset(_14_out));  // open: preset, en
  D_Flip_Flop bit_3 (
    .clk(bit_2_qn), .D(bit_3_qn), .Q(\output [2]), .Qn(bit_3_qn), .reset(_14_out));  // open: preset, en
  D_Flip_Flop bit_4 (
    .clk(bit_3_qn), .D(bit_4_qn), .Q(\output [3]), .Qn(bit_4_qn), .reset(_14_out));  // open: preset, en
  and _14 (_14_out, \output [3], \output [2], \output [1], not_1_out);
  not not_1 (not_1_out, \output [0]);
endmodule

module Controller (
  input  [3:0] \input ,
  output State_3_pin,
  output State_2_pin,
  output State_1_pin,
  output State_4_pin,
  output State_5_pin
);

  wire _3_out, _4_out, _5_out, _6_out, _7_out, _8_out, _9_out, _10_out, _11_out, _12_out, _13_out, ALL_out,
       not_1_out, not_2_out, not_3_out, not_4_out, not_5_out, not_6_out, not_7_out, not_8_out, not_9_out,
       not_10_out, not_11_out, not_12_out, not_13_out, not_14_out, not_15_out, not_16_out, not_17_out,
       not_18_out;

  not not_1 (not_1_out, \input [0]);
  not not_2 (not_2_out, \input [1]);
  not not_3 (not_3_out, \input [3]);
  not not_4 (not_4_out, \input [0]);
  not not_5 (not_5_out, \input [1]);
  not not_6 (not_6_out, \input [2]);
  not not_7 (not_7_out, \input [3]);
  not not_8 (not_8_out, \input [1]);
  not not_9 (not_9_out, \input [2]);
  not not_10 (not_10_out, \input [0]);
  not not_11 (not_11_out, \input [1]);
  not not_12 (not_12_out, \input [2]);
  not not_13 (not_13_out, \input [3]);
  not not_14 (not_14_out, \input [0]);
  not not_15 (not_15_out, \input [1]);
  not not_16 (not_16_out, \input [2]);
  and _5 (_5_out, not_3_out, \input [2], \input [0], not_2_out);
  and _6 (_6_out, \input [1], \input [2], not_3_out, not_1_out, not_1_out);
  and _3 (_3_out, not_7_out, \input [0], not_6_out, \input [1]);
  and _4 (_4_out, \input [2], not_5_out, not_7_out, not_4_out);
  and _11 (_11_out, \input [3], \input [0], not_9_out, \input [1]);
  and _13 (_13_out, \input [2], not_8_out, \input [3], \input [0]);
  and _7 (_7_out, not_13_out, \input [0], \input [2], \input [1]);
  and _8 (_8_out, not_10_out, \input [3], not_11_out, not_12_out);
  and _9 (_9_out, not_15_out, not_16_out, \input [0], \input [3]);
  and _10 (_10_out, not_16_out, \input [3], \input [1], not_14_out);
  or S3 (State_3_pin, _5_out, _11_out, _13_out, _6_out);
  or S2 (State_2_pin, _3_out, _11_out, _13_out, _4_out);
  xor S1 (State_1_pin, ALL_out, _12_out);
  not not_17 (not_17_out, \input [0]);
  not not_18 (not_18_out, \input [1]);
  or S4 (State_4_pin, _7_out, _13_out, _11_out, _8_out);
  or S5 (State_5_pin, _9_out, _13_out, _11_out, _10_out);
  or ALL (ALL_out, \input [0], \input [2], \input [3], \input [1]);
  and _12 (_12_out, not_17_out, \input [2], not_18_out, \input [3]);
endmodule
